# Fritzing sketch connection diagram (saved by Fritzing 1.0.2b)
breadboards: 1

parts:
  DS1 = DS18B20_Probe_Cable
  Mod1 = DFRobot_Mega_Sensor_Shield_v2.4_1
  Mod1_0 = DFRobot_Mega_Sensor_Shield_v2.4 [package=THT]  # not connected
  Mod1_1 = DFRobot_Mega_Sensor_Shield_v2.4 [package=THT]  # not connected
  Mod1_2 = DFRobot_Mega_Sensor_Shield_v2.4 [package=THT]  # not connected
  Mod1_3 = DFRobot_Mega_Sensor_Shield_v2.4 [package=THT]  # not connected
  Mod1_4 = DFRobot_Mega_Sensor_Shield_v2.4 [package=THT]  # not connected
  Mod1_5 = DFRobot_Mega_Sensor_Shield_v2.4 [package=THT]  # not connected
  Mod1_6 = DFRobot_Mega_Sensor_Shield_v2.4 [package=THT]  # not connected
  Mod1_7 = DFRobot_Mega_Sensor_Shield_v2.4 [package=THT]  # not connected
  Mod1_8 = DFRobot_Mega_Sensor_Shield_v2.4 [package=THT]  # not connected
  Mod1_9 = DFRobot_Mega_Sensor_Shield_v2.4 [package=THT]  # not connected
  Mod1_10 = DFRobot_Mega_Sensor_Shield_v2.4 [package=THT]  # not connected
  Mod1_11 = DFRobot_Mega_Sensor_Shield_v2.4 [package=THT]  # not connected
  Mod1_12 = DFRobot_Mega_Sensor_Shield_v2.4 [package=THT]  # not connected
  Mod1_13 = DFRobot_Mega_Sensor_Shield_v2.4 [package=THT]  # not connected
  Mod1_14 = DFRobot_Mega_Sensor_Shield_v2.4 [package=THT]  # not connected
  Mod1_15 = DFRobot_Mega_Sensor_Shield_v2.4 [package=THT]  # not connected
  Mod1_16 = DFRobot_Mega_Sensor_Shield_v2.4 [package=THT]  # not connected
  Mod1_17 = DFRobot_Mega_Sensor_Shield_v2.4 [package=THT]  # not connected
  Mod1_18 = DFRobot_Mega_Sensor_Shield_v2.4 [package=THT]  # not connected
  Mod1_19 = DFRobot_Mega_Sensor_Shield_v2.4 [package=THT]  # not connected
  Mod1_20 = DFRobot_Mega_Sensor_Shield_v2.4 [package=THT]  # not connected
  Mod1_21 = DFRobot_Mega_Sensor_Shield_v2.4 [package=THT]  # not connected
  DS2 = DS18B20_Probe_Cable
  A1 = JXBS-3001-NPK-RS
  M1 = MAX485 Breakout [package=THT]
  A2 = Oxygen / O2 Sensor
  Capacitive_Soil_Moisture_Sensor1 = DFRobot Capacitive Soil Moisture Sensor V1.0 [part_number=SEN0193]
  A3 = MG881 CO2 Sensor
  Part1 = MQ-3 breakout
  VCC1 = Battery block 9V
  R1 = Resistor [tolerance=±5% power=0.25W resistance=4700 package=THT]
  A4 = xkc-25y-v [package=THT]
  A5 = SEN0204
  A6 = DM860A Stepper Motor Driver
  Power_plug1 = Power plug
  M2 = Stepper Motor - Bipolar

nets:
  N1: DS1.connector1, DS2.connector1, A1.Pin_2, M1.GND, VCC1.-, A6.DIR+(+5V)
  N2: DS1.connector2, Mod1.connector108, Mod1.connector111, DS2.connector2, R1.Pin_0
  N3: DS1.connector3, DS2.connector3, M1.VCC, R1.Pin_1, A6.ENBL+(+5V), A6.PUL+(+5V)
  N4: Mod1.connector94, A4.pin3, A5.pin_3, A5.pin_7
  N5: Mod1.connector95, A4.pin1, A5.pin_1, A5.pin_6
  N6: Mod1.connector96, A4.pin2, A5.pin_2, A5.pin_5
  N7: Mod1.connector144, A3.Pin_3
  N8: Mod1.connector145, A3.Pin_2
  N9: Mod1.connector146, A3.Pin_1
  N10: Mod1.connector147, Part1.GND
  N11: Mod1.connector148, Part1.VCC
  N12: Mod1.connector149, Part1.AO
  N13: Mod1.connector150, Capacitive_Soil_Moisture_Sensor1.GND
  N14: Mod1.connector151, Capacitive_Soil_Moisture_Sensor1.VCC
  N15: Mod1.connector152, Capacitive_Soil_Moisture_Sensor1.A
  N16: Mod1.connector290, M1.DI
  N17: Mod1.connector291, M1.RO
  N18: Mod1.connector293, M1.RE
  N19: Mod1.connector294, M1.DE
  N20: Mod1.connector307, A6.PUL-(PUL)
  N21: Mod1.connector310, A6.DIR-(DIR)
  N22: Mod1.connector313, A6.ENBL-(ENB)
  N23: Mod1.connector350, A2.Pin_1
  N24: Mod1.connector351, A2.Pin_2
  N25: Mod1.connector352, A2.Pin_3
  N26: Mod1.connector353, A2.Pin_4
  N27: A1.Pin_1, VCC1.+
  N28: A1.Pin_3, M1.A1
  N29: A1.Pin_4, M1.B1
  N30: A4.pin4, A5.pin_4
  N31: A6.B-, M2.D
  N32: A6.B+, M2.B
  N33: A6.A-, M2.C
  N34: A6.A+, M2.A
  N35: A6.VDC, Power_plug1.VCC
  GND: A6.GND, Power_plug1.GND

custom parts:
  DFRobot_Mega_Sensor_Shield_v2.4: DFRobot Mega Sensor Shield v2.4. Note pcb has been omitted as unneeded, and schematic is subparts (so you can move the parts you are using around in schematic and store the unused parts to save schematic space.) This will likely slow Fritzing down, and means the part is not bused, so connected pins will not light up when clicked. Based on Stephen Parry's breadboard svg from the DFR site.
  DFRobot_Mega_Sensor_Shield_v2.4: DFRobot Mega Sensor Shield v2.4. Note pcb has been omitted as unneeded, and schematic is subparts (so you can move the parts you are using around in schematic and store the unused parts to save schematic space.) This will likely slow Fritzing down, and means the part is not bused, so connected pins will not light up when clicked. Based on Stephen Parry's breadboard svg from the DFR site.
  DFRobot_Mega_Sensor_Shield_v2.4: DFRobot Mega Sensor Shield v2.4. Note pcb has been omitted as unneeded, and schematic is subparts (so you can move the parts you are using around in schematic and store the unused parts to save schematic space.) This will likely slow Fritzing down, and means the part is not bused, so connected pins will not light up when clicked. Based on Stephen Parry's breadboard svg from the DFR site.
  DFRobot_Mega_Sensor_Shield_v2.4: DFRobot Mega Sensor Shield v2.4. Note pcb has been omitted as unneeded, and schematic is subparts (so you can move the parts you are using around in schematic and store the unused parts to save schematic space.) This will likely slow Fritzing down, and means the part is not bused, so connected pins will not light up when clicked. Based on Stephen Parry's breadboard svg from the DFR site.
  DFRobot_Mega_Sensor_Shield_v2.4: DFRobot Mega Sensor Shield v2.4. Note pcb has been omitted as unneeded, and schematic is subparts (so you can move the parts you are using around in schematic and store the unused parts to save schematic space.) This will likely slow Fritzing down, and means the part is not bused, so connected pins will not light up when clicked. Based on Stephen Parry's breadboard svg from the DFR site.
  DFRobot_Mega_Sensor_Shield_v2.4: DFRobot Mega Sensor Shield v2.4. Note pcb has been omitted as unneeded, and schematic is subparts (so you can move the parts you are using around in schematic and store the unused parts to save schematic space.) This will likely slow Fritzing down, and means the part is not bused, so connected pins will not light up when clicked. Based on Stephen Parry's breadboard svg from the DFR site.
  DFRobot_Mega_Sensor_Shield_v2.4: DFRobot Mega Sensor Shield v2.4. Note pcb has been omitted as unneeded, and schematic is subparts (so you can move the parts you are using around in schematic and store the unused parts to save schematic space.) This will likely slow Fritzing down, and means the part is not bused, so connected pins will not light up when clicked. Based on Stephen Parry's breadboard svg from the DFR site.
  DFRobot_Mega_Sensor_Shield_v2.4: DFRobot Mega Sensor Shield v2.4. Note pcb has been omitted as unneeded, and schematic is subparts (so you can move the parts you are using around in schematic and store the unused parts to save schematic space.) This will likely slow Fritzing down, and means the part is not bused, so connected pins will not light up when clicked. Based on Stephen Parry's breadboard svg from the DFR site.
  DFRobot_Mega_Sensor_Shield_v2.4: DFRobot Mega Sensor Shield v2.4. Note pcb has been omitted as unneeded, and schematic is subparts (so you can move the parts you are using around in schematic and store the unused parts to save schematic space.) This will likely slow Fritzing down, and means the part is not bused, so connected pins will not light up when clicked. Based on Stephen Parry's breadboard svg from the DFR site.
  DFRobot_Mega_Sensor_Shield_v2.4: DFRobot Mega Sensor Shield v2.4. Note pcb has been omitted as unneeded, and schematic is subparts (so you can move the parts you are using around in schematic and store the unused parts to save schematic space.) This will likely slow Fritzing down, and means the part is not bused, so connected pins will not light up when clicked. Based on Stephen Parry's breadboard svg from the DFR site.
  DFRobot_Mega_Sensor_Shield_v2.4: DFRobot Mega Sensor Shield v2.4. Note pcb has been omitted as unneeded, and schematic is subparts (so you can move the parts you are using around in schematic and store the unused parts to save schematic space.) This will likely slow Fritzing down, and means the part is not bused, so connected pins will not light up when clicked. Based on Stephen Parry's breadboard svg from the DFR site.
  DFRobot_Mega_Sensor_Shield_v2.4: DFRobot Mega Sensor Shield v2.4. Note pcb has been omitted as unneeded, and schematic is subparts (so you can move the parts you are using around in schematic and store the unused parts to save schematic space.) This will likely slow Fritzing down, and means the part is not bused, so connected pins will not light up when clicked. Based on Stephen Parry's breadboard svg from the DFR site.
  DFRobot_Mega_Sensor_Shield_v2.4: DFRobot Mega Sensor Shield v2.4. Note pcb has been omitted as unneeded, and schematic is subparts (so you can move the parts you are using around in schematic and store the unused parts to save schematic space.) This will likely slow Fritzing down, and means the part is not bused, so connected pins will not light up when clicked. Based on Stephen Parry's breadboard svg from the DFR site.
  DFRobot_Mega_Sensor_Shield_v2.4: DFRobot Mega Sensor Shield v2.4. Note pcb has been omitted as unneeded, and schematic is subparts (so you can move the parts you are using around in schematic and store the unused parts to save schematic space.) This will likely slow Fritzing down, and means the part is not bused, so connected pins will not light up when clicked. Based on Stephen Parry's breadboard svg from the DFR site.
  DFRobot_Mega_Sensor_Shield_v2.4: DFRobot Mega Sensor Shield v2.4. Note pcb has been omitted as unneeded, and schematic is subparts (so you can move the parts you are using around in schematic and store the unused parts to save schematic space.) This will likely slow Fritzing down, and means the part is not bused, so connected pins will not light up when clicked. Based on Stephen Parry's breadboard svg from the DFR site.
  DFRobot_Mega_Sensor_Shield_v2.4: DFRobot Mega Sensor Shield v2.4. Note pcb has been omitted as unneeded, and schematic is subparts (so you can move the parts you are using around in schematic and store the unused parts to save schematic space.) This will likely slow Fritzing down, and means the part is not bused, so connected pins will not light up when clicked. Based on Stephen Parry's breadboard svg from the DFR site.
  DFRobot_Mega_Sensor_Shield_v2.4: DFRobot Mega Sensor Shield v2.4. Note pcb has been omitted as unneeded, and schematic is subparts (so you can move the parts you are using around in schematic and store the unused parts to save schematic space.) This will likely slow Fritzing down, and means the part is not bused, so connected pins will not light up when clicked. Based on Stephen Parry's breadboard svg from the DFR site.
  DFRobot_Mega_Sensor_Shield_v2.4: DFRobot Mega Sensor Shield v2.4. Note pcb has been omitted as unneeded, and schematic is subparts (so you can move the parts you are using around in schematic and store the unused parts to save schematic space.) This will likely slow Fritzing down, and means the part is not bused, so connected pins will not light up when clicked. Based on Stephen Parry's breadboard svg from the DFR site.
  DFRobot_Mega_Sensor_Shield_v2.4: DFRobot Mega Sensor Shield v2.4. Note pcb has been omitted as unneeded, and schematic is subparts (so you can move the parts you are using around in schematic and store the unused parts to save schematic space.) This will likely slow Fritzing down, and means the part is not bused, so connected pins will not light up when clicked. Based on Stephen Parry's breadboard svg from the DFR site.
  DFRobot_Mega_Sensor_Shield_v2.4: DFRobot Mega Sensor Shield v2.4. Note pcb has been omitted as unneeded, and schematic is subparts (so you can move the parts you are using around in schematic and store the unused parts to save schematic space.) This will likely slow Fritzing down, and means the part is not bused, so connected pins will not light up when clicked. Based on Stephen Parry's breadboard svg from the DFR site.
  DFRobot_Mega_Sensor_Shield_v2.4: DFRobot Mega Sensor Shield v2.4. Note pcb has been omitted as unneeded, and schematic is subparts (so you can move the parts you are using around in schematic and store the unused parts to save schematic space.) This will likely slow Fritzing down, and means the part is not bused, so connected pins will not light up when clicked. Based on Stephen Parry's breadboard svg from the DFR site.
  DFRobot_Mega_Sensor_Shield_v2.4: DFRobot Mega Sensor Shield v2.4. Note pcb has been omitted as unneeded, and schematic is subparts (so you can move the parts you are using around in schematic and store the unused parts to save schematic space.) This will likely slow Fritzing down, and means the part is not bused, so connected pins will not light up when clicked. Based on Stephen Parry's breadboard svg from the DFR site.
  JXBS-3001-NPK-RS: The NPK sensor is designed for detecting the content of nitrogen, phosphorus and potassium in soil, determining the fertility of the soil and facilitating the evaluation of the soil condition by the customer system.
  MAX485 Breakout: MAX485 RS485 breakout board
  Oxygen / O2 Sensor: This Oxygen / O2 Sensor is based on electrochemical principles and it can measure the ambient O2 concentration accurately and conveniently.
  DFRobot Capacitive Soil Moisture Sensor V1.0: DFRobot Capacitive Soil Moisture Sensor V1.0 This product measures soil moisture levels by capacitive sensing, rather than resistive sensing like other types of moisture sensor. It is made of a corrosion resistant material giving it a long service life. Insert it into soil and impress your friends with the real-time soil moisture data! The product includes an on-board voltage regulator which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
  MG881 CO2 Sensor: This is the first CO2 sensor in the Arduino market. The output voltage of the module falls as the concentration of the CO2 increases.
  MQ-3 breakout: Alcohol sensor is capable of detecting alcohol (ethanol) particles on itself and gives the information in digital form back to us to manipulate with it. SKU:101251 • Voltage: 5V DC • Power: max 750mW • Measurement range: 0.04-4mg/L
  xkc-25y-v: XKC-Y25-v Non-Contact Liquid Level Sensor IP67 Waterproof Water Level Detector DC 5-12V. Note this version has the plug reversed to match the connector on the DFrobot sens0204 interface board, thus the connector labels on the device are opposite of the connectors on the output connector.
  SEN0204: This is a non-contact water / liquid level sensor for Arduino. It utilizes advanced signal processing technology by using a powerful chip (XKC-Y25-T12V) with high-speed operation capacity to achieve non-contact liquid level detection. No contact with liquid makes the module suitable for hazardous applications such as detecting toxic substances, strong acid, strong alkali, and all kinds of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
  DM860A Stepper Motor Driver: DM860A is a type of two-phase hybrid stepping motor driver, The drive voltage of which is from 24VDC to 80VDC. It is designed for use with 2-phase hybrid stepper motor of all kinds with 57mm to 110mm outside diameter and less than 8.0A phase current. Mar 2023: Correct pcb layerId as the part won't save correctly in a .fzz file as is.
